// Logisim project MIPSProcessor.circ as structural Verilog
module MIPS32 (
);

  // MIPSProgramROM mipsprogramrom_1: pin names not known
  // Incrementer incrementer_1: pin names not known
  // Mips_ALU mips_alu_1: pin names not known
  // RegisterFile registerfile_1: pin names not known
endmodule

module instructionFetch (
  input  Stall,
  output [31:0] inst,
  output [31:0] PCPlus4
);

  wire clock_1_out;
  wire [31:2] register_1_q;

  Register #(.width(32)) register_1 (
    .D(PCPlus4), .en(Stall), .clk(clock_1_out), .Q({register_1_q, PCPlus4[1:0]}));  // open: clr
  Clock clock_1 (.out(clock_1_out));
  // Incrementer #(.width(30)) incrementer_1: pin names not known; wires that end beside it: Stall, register_1_q, PCPlus4[31:2]
  // MIPSProgramROM mipsprogramrom_1: pin names not known; wires that end beside it: {register_1_q, PCPlus4[1:0]}, inst
endmodule
